// Digital circuit CPU_main.dig as structural Verilog
module CPU_main (
);

  ALU_main alu_main_1 ();  // open: A_in, B_in, ALU_op, CLK, START, S_out, Z_flag, ALU_busy
  Register #(.Bits(8)) Acc ();  // open: D, C, en, Q
  ROM #(.AddrBits(8), .Bits(8)) ROM ();  // open: A, sel, D
  Register #(.Bits(8)) B_reg ();  // open: D, C, en, Q
  Register #(.Bits(8)) IR ();  // open: D, C, en, Q
  CounterPreset PC ();  // open: en, C, dir, in, ld, clr, out, ovf
  Register #(.Bits(8)) Out_reg ();  // open: D, C, en, Q
  Register #(.Bits(8)) MAR ();  // open: D, C, en, Q
endmodule
